# Fritzing sketch mainboard (saved by Fritzing 0.9.3b)
circuit board: 5.17612cm x 5.2cm
breadboards: 1

parts:
  ADS_1115 = Adafruit ADS1115 16Bit I2C ADC [part_number="Adafruit #1085"]
  PWR = Battery block 9V
  Cel_O2 = Header 2 [package=molex-1x2_lock]
  Buzz = Piezo Speaker
  VideoSub_2020_OxyMetre_|_GNU/GPL = Arduino Nano (Rev3.0)
  OLED = Grove OLED 128x96

nets:
  N1: ADS_1115.AIN1, Cel_O2.1
  N2: ADS_1115.AIN0, Cel_O2.2
  N3: ADS_1115.SDA, VideoSub_2020_OxyMetre_|_GNU/GPL.A4, OLED.SDA
  N4: ADS_1115.SCL, VideoSub_2020_OxyMetre_|_GNU/GPL.A5, OLED.SCL
  GND: ADS_1115.GND, PWR.-, Buzz.pin1, VideoSub_2020_OxyMetre_|_GNU/GPL.GND, OLED.GND
  VDD: ADS_1115.VDD, PWR.+, VideoSub_2020_OxyMetre_|_GNU/GPL.5V, OLED.VCC
  N5: Buzz.pin2, VideoSub_2020_OxyMetre_|_GNU/GPL.D9

custom parts:
  Adafruit ADS1115 16Bit I2C ADC: For microcontrollers without an analog-to-digital converter or when you want a higher-precision ADC, the ADS1115 provides 16-bit precision at 860 samples/second over I2C. The chip can be configured as 4 single-ended input channels, or two differential channels. As a nice bonus, it even includes a programmable gain amplifier, up to x16, to help boost up smaller single/differential signals to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
