# Fritzing sketch mainboard-01 (saved by Fritzing 0.9.3b)
circuit board: 7.95cm x 10.5cm
breadboards: 1

parts:
  ADS_1115 = Adafruit ADS1115 16Bit I2C ADC [part_number="Adafruit #1085"]
  OXY = Header 2 [package=molex-1x2_lock]
  IC2_PWR = TL074 Quad Opamp (Movable) [package="DIP (Dual Inline)"]  # not connected
  IC2_B = TL074 Quad Opamp (Movable) [package="DIP (Dual Inline)"]  # not connected
  IC2_C = TL074 Quad Opamp (Movable) [package="DIP (Dual Inline)"]  # not connected
  IC2_D = TL074 Quad Opamp (Movable) [package="DIP (Dual Inline)"]  # not connected
  IC1_PWR = TL074 Quad Opamp (Movable) [package="DIP (Dual Inline)"]  # not connected
  IC1_A = TL074 Quad Opamp (Movable) [package="DIP (Dual Inline)"]  # not connected
  IC1_B = TL074 Quad Opamp (Movable) [package="DIP (Dual Inline)"]  # not connected
  IC1_C = TL074 Quad Opamp (Movable) [package="DIP (Dual Inline)"]  # not connected
  IC1_D = TL074 Quad Opamp (Movable) [package="DIP (Dual Inline)"]  # not connected
  IC1_PWR_2 = TL074 Quad Opamp (Movable) [package="DIP (Dual Inline)"]  # not connected
  IC1_A_2 = TL074 Quad Opamp (Movable) [package="DIP (Dual Inline)"]  # not connected
  IC1_B_2 = TL074 Quad Opamp (Movable) [package="DIP (Dual Inline)"]  # not connected
  IC1_C_2 = TL074 Quad Opamp (Movable) [package="DIP (Dual Inline)"]  # not connected
  IC1_D_2 = TL074 Quad Opamp (Movable) [package="DIP (Dual Inline)"]  # not connected
  Arduino_Nano = Arduino Nano (Rev3.0)
  BAT_18650 = 18650 battery holder [package=battery-18650-kit]
  TP1 = TP4056 [chip_label="TP4056 USB Charger" package="DIP (Dual Inline) [THT]"]
  OUT+ = rounded female pin header, 1 pin [form="♀ (female rounded)"]
  OUT- = rounded female pin header, 1 pin [form="♀ (female rounded)"]
  VIN+ = rounded female pin header, 1 pin [form="♀ (female rounded)"]
  VIN- = rounded female pin header, 1 pin [form="♀ (female rounded)"]
  R_2kΩ = Resistor [tolerance=±5% resistance=220 package=THT]
  R_2kΩ_2 = Resistor [tolerance=±5% resistance=220 package=THT]
  check = Header 2 [package=molex-1x2_lock]
  1N400X = Diode [package=diode-1n4148]
  on/off = Header 2 [package=molex-1x2_lock]
  1N400X_2 = Diode [package=diode-1n4148]
  MD62 = Header 4 [package=molex-1x4_lock]
  Ext_A = female pin header, 4 pins [form="♀ (female)"]
  Ext_D = double row female pin header, 20 pins [form="♀ (female)"]
  OLED = female pin header, 4 pins [form="♀ (female)"]
  500Ω = female pin header, 3 pins [form="♀ (female)"]
  J1 = double row male pin header, 4 pins [form="♂ (male)"]
  LM2596 = LM2596 step down module

nets (from the pcb view):
  N1: ADS_1115.AIN3, check.2, J1.pin4
  N2: ADS_1115.AIN2, check.1, J1.pin1
  N3: ADS_1115.AIN1, OXY.1
  N4: ADS_1115.AIN0, OXY.2
  N5: ADS_1115.SDA, Arduino_Nano.A5, OLED.pin4
  N6: ADS_1115.SCL, Arduino_Nano.A4, OLED.pin3
  GND: ADS_1115.GND, Arduino_Nano.GND, TP1.pin2, OUT-.pin1, R_2kΩ_2.Pin_0, MD62.4, Ext_D.pin11, Ext_D.pin12, Ext_D.pin13, Ext_D.pin14, Ext_D.pin15, Ext_D.pin16, Ext_D.pin17, Ext_D.pin18, Ext_D.pin19, Ext_D.pin20, OLED.pin2
  VDD: ADS_1115.VDD, Arduino_Nano.5V, OUT+.pin1, OLED.pin1, LM2596.IN+
  N7: Arduino_Nano.D2, Ext_D.pin9
  N8: Arduino_Nano.D3, Ext_D.pin8
  N9: Arduino_Nano.D4, Ext_D.pin7
  N10: Arduino_Nano.D5, Ext_D.pin6
  N11: Arduino_Nano.D6, Ext_D.pin5
  N12: Arduino_Nano.D7, Ext_D.pin4
  N13: Arduino_Nano.D8, Ext_D.pin3
  N14: Arduino_Nano.D9, Ext_D.pin2
  N15: Arduino_Nano.D10, Ext_D.pin1
  N16: Arduino_Nano.A3, Ext_A.pin1
  N17: Arduino_Nano.A2, Ext_A.pin2
  N18: Arduino_Nano.A1, Ext_A.pin3
  N19: Arduino_Nano.A0, Ext_A.pin4
  N20: BAT_18650.+, TP1.pin4
  N21: BAT_18650.-, TP1.pin5
  N22: TP1.pin1, 1N400X.A
  N23: TP1.pin3, 1N400X_2.A
  N24: TP1.pin6, VIN-.pin1
  N25: VIN+.pin1, on/off.1
  N26: R_2kΩ.Pin_0, MD62.1, LM2596.IN-, LM2596.OUT-
  N27: R_2kΩ.Pin_1, 500Ω.pin1
  N28: R_2kΩ_2.Pin_1, 500Ω.pin3
  N29: 1N400X.C, on/off.2, 1N400X_2.C
  N30: MD62.2, MD62.3, J1.pin2
  N31: 500Ω.pin2, J1.pin3

notes:
  gasblender.org
  Code GNU/GPL v3+
  usb →
  MT3608 DC-DC Booster
  USB
  (c) 2020 - Eric Seigne
  Output = 5V
  GND
  VIN
  SCL
  SDA
  AIN0
  AIN1
  AIN2
  AIN3
  5V
  A5
  A4
  +
  -
  BUZZ
  R.Var
  * J1: mettre des jumper pour activer le MD62
  * check: pour pouvoir brancher le multimètre pour calibrer la resistance variable de 500Ω
  * check: pourrait être utilisé pour connecter le tube ultrason si on a du bol a la place de la MD62
  * OXY : sonde oxy
  * OLED: écran
  * Ext A : pour pouvoir connecter de futurs dispositifs sur les broches A de l'arduino
  * Ext D: pour pouvoir connecter de futurs dispositifs sur les broches D de l'arduino
  -> D9 pour le buzzer
  * on/off pour eviter d'alimenter le DC Boost tout le temps
  * les 1N400X pour éviter le retour quand la prise usb est branchée
  * Note: souder le LM2596 uniquement pour la version trimix
  A3
  A2
  A1
  A0
  D2
  D7
  D10
  D8
  D4
  D3
  D9
  GND →
  D6
  D5
  ← GND
  Design CC-BY-SA
  Output = 3V
  version 20200929

custom parts:
  Adafruit ADS1115 16Bit I2C ADC: For microcontrollers without an analog-to-digital converter or when you want a higher-precision ADC, the ADS1115 provides 16-bit precision at 860 samples/second over I2C. The chip can be configured as 4 single-ended input channels, or two differential channels. As a nice bonus, it even includes a programmable gain amplifier, up to x16, to help boost up smaller single/differential signals to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
  TL074 Quad Opamp (Movable): Quadruple Operational Amplifier (Opamp)
  TL074 Quad Opamp (Movable): Quadruple Operational Amplifier (Opamp)
  TL074 Quad Opamp (Movable): Quadruple Operational Amplifier (Opamp)
  TL074 Quad Opamp (Movable): Quadruple Operational Amplifier (Opamp)
  TL074 Quad Opamp (Movable): Quadruple Operational Amplifier (Opamp)
  18650 battery holder: 18650 Battery Holder
  TP4056: A DIP stand-in part for whatever IC you want. With 6 pins on a 300mil dual inline package (DIP) footprint.
  LM2596 step down module: LM2596 DC-DC step down power supply module 3 A.
